# Fritzing sketch schematic (saved by Fritzing 1.0.6)
breadboards: 1

parts:
  TCS1 = TCS3200
  Part1 = Arduino Uno (Rev3) - ICSP
  J1 = Basic Servo
  J2 = Basic Servo
  VCC1 = 4 x AAA Battery Mount [internal_resistance=0.1Ω]

nets:
  N1: TCS1.S1, Part1.D3_PWM
  N2: TCS1.S0, Part1.D2
  GND: TCS1.GND, Part1.GND, J1.gnd, J2.gnd, VCC1.-
  N3: TCS1.OUT, Part1.D6_PWM
  N4: TCS1.S2, Part1.D4
  N5: TCS1.S3, Part1.D5_PWM
  VCC: TCS1.VCC, Part1.5V
  N6: Part1.D8, J2.pulse
  N7: Part1.D7, J1.pulse
  VCC_2: J1.vcc, J2.vcc, VCC1.+

custom parts:
  TCS3200: COLOR SENSING TCS3200
